// Logisim project Vertabrate32bit.circ as structural Verilog
module Vertebrate32 (
  input  [1:0] DATA_MUX,
  input  [31:0] DATA_IN,
  input  [1:0] AR_MUX,
  input  IR_LD,
  input  PC_LOAD,
  input  PC_INC,
  input  CU_RGLD,
  input  PC_MUX,
  input  CU_MUX
);

  wire alu_32_bit_1_equal;
  wire [2:0] instruction_register_1_ir_out;
  wire [27:0] adder_1_out, multiplexer_1_out, multiplexer_2_out, multiplexer_6_out, programcounter_1_ir_out,
       registerbank32_1_dout8;
  wire [27:3] instruction_register_1_ir_out_2;
  wire [31:0] alu_32_bit_1_output, four_bit_extender_1_xtender_output, multiplexer_3_out, multiplexer_4_out,
       multiplexer_5_out, registerbank32_1_dout1, registerbank32_1_dout2, registerbank32_1_dout3,
       registerbank32_1_dout4, registerbank32_1_dout5, registerbank32_1_dout6, registerbank32_1_dout7,
       thirtyone_bit_extender_1_xtender_out;
  wire [31:28] multiplexer_6_out_2, registerbank32_1_dout8_2;

  Adder #(.width(28)) adder_1 (
    .a(programcounter_1_ir_out), .b({instruction_register_1_ir_out_2, instruction_register_1_ir_out}),
    .out(adder_1_out));  // open: cin, cout
  Multiplexer #(.select(2), .width(28)) multiplexer_1 (
    .in0(programcounter_1_ir_out), .in1(multiplexer_6_out), .in2(registerbank32_1_dout8),
    .out(multiplexer_1_out), .sel(AR_MUX));  // open: in3
  ProgramCounter programcounter_1 (
    .PC_LD(PC_LOAD), .IR_INPUT(multiplexer_2_out), .PC_INC(PC_INC), .IR_OUT(programcounter_1_ir_out));
  Multiplexer #(.width(28)) multiplexer_2 (
    .in0(adder_1_out), .in1(DATA_IN[27:0]), .out(multiplexer_2_out), .sel(PC_MUX));
  FOUR_BIT_EXTENDER four_bit_extender_1 (
    .Xtender_input(programcounter_1_ir_out), .Xtender_output(four_bit_extender_1_xtender_output));
  RegisterBank32 registerbank32_1 (
    .RegLoad(CU_RGLD), .RegSelect(instruction_register_1_ir_out), .Data_In(multiplexer_4_out),
    .DOUT2(registerbank32_1_dout2), .DOUT3(registerbank32_1_dout3), .DOUT4(registerbank32_1_dout4),
    .DOUT1(registerbank32_1_dout1), .DOUT5(registerbank32_1_dout5), .DOUT6(registerbank32_1_dout6),
    .DOUT7(registerbank32_1_dout7), .DOUT8({registerbank32_1_dout8_2, registerbank32_1_dout8}));  // open: SPnn, SPpp
  Multiplexer #(.select(2), .width(32)) multiplexer_3 (
    .in0(multiplexer_5_out), .in1(four_bit_extender_1_xtender_output),
    .in2(thirtyone_bit_extender_1_xtender_out), .out(multiplexer_3_out), .sel(DATA_MUX));  // open: in3
  Thirtyone_BIT_EXTENDER thirtyone_bit_extender_1 (
    .Xtender_IN(alu_32_bit_1_equal), .Xtender_out(thirtyone_bit_extender_1_xtender_out));
  Multiplexer #(.width(32)) multiplexer_4 (
    .in0(alu_32_bit_1_output), .in1(DATA_IN), .out(multiplexer_4_out), .sel(CU_MUX));
  Multiplexer #(.select(3), .width(32)) multiplexer_5 (
    .in0(registerbank32_1_dout1), .in1(registerbank32_1_dout2), .in2(registerbank32_1_dout3),
    .in3(registerbank32_1_dout4), .in4(registerbank32_1_dout5), .in5(registerbank32_1_dout6),
    .in6(registerbank32_1_dout7), .in7({registerbank32_1_dout8_2, registerbank32_1_dout8}),
    .out(multiplexer_5_out), .sel(instruction_register_1_ir_out_2[8:6]));
  ALU_32_Bit alu_32_bit_1 (
    .ALUCODE(instruction_register_1_ir_out_2[27:23]), .Input_1(multiplexer_5_out),
    .Input_2({multiplexer_6_out_2, multiplexer_6_out}), .OUTPUT(alu_32_bit_1_output),
    .EQUAL(alu_32_bit_1_equal));  // open: NOT_EQUAL, LESS_THAN, LESS_OR_EQUAL, GREATER_THAN, OVERFLOW, GREATER_OR_EQUAL
  Multiplexer #(.select(3), .width(32)) multiplexer_6 (
    .in0(registerbank32_1_dout1), .in1(registerbank32_1_dout2), .in2(registerbank32_1_dout3),
    .in3(registerbank32_1_dout4), .in4(registerbank32_1_dout5), .in5(registerbank32_1_dout6),
    .in6(registerbank32_1_dout7), .in7({registerbank32_1_dout8_2, registerbank32_1_dout8}),
    .out({multiplexer_6_out_2, multiplexer_6_out}), .sel(instruction_register_1_ir_out_2[5:3]));
  INSTRUCTION_REGISTER instruction_register_1 (
    .IR_LD(IR_LD), .IR_INPUT(DATA_IN[27:0]),
    .IR_OUT({instruction_register_1_ir_out_2, instruction_register_1_ir_out}));

  // Notes on the sheet:
  //   To Address Bus 28'b
  //   DATA OUT 32'b
  //   IF ZF UNIT WANTED ADD HERE
endmodule

module RegisterBank32 (
  input  [2:0] RegSelect,
  input  RegLoad,
  input  [31:0] Data_In,
  input  SPnn,
  input  SPpp,
  output [31:0] DOUT1,
  output [31:0] DOUT2,
  output [31:0] DOUT3,
  output [31:0] DOUT4,
  output [31:0] DOUT5,
  output [31:0] DOUT6,
  output [31:0] DOUT7,
  output [31:0] DOUT8
);

  wire and_1_out, and_2_out, and_3_out, and_4_out, and_5_out, and_6_out, and_7_out, and_8_out,
       decoder_1_out0, decoder_1_out1, decoder_1_out2, decoder_1_out3, decoder_1_out4, decoder_1_out5,
       decoder_1_out6, decoder_1_out7;

  Decoder #(.enable("false"), .select(3)) decoder_1 (
    .out0(decoder_1_out0), .out1(decoder_1_out1), .out2(decoder_1_out2), .out3(decoder_1_out3),
    .out4(decoder_1_out4), .out5(decoder_1_out5), .out6(decoder_1_out6), .out7(decoder_1_out7),
    .sel(RegSelect));
  and and_1 (and_1_out, decoder_1_out0, RegLoad);
  and and_2 (and_2_out, decoder_1_out1, RegLoad);
  and and_3 (and_3_out, decoder_1_out2, RegLoad);
  and and_4 (and_4_out, decoder_1_out3, RegLoad);
  and and_5 (and_5_out, decoder_1_out4, RegLoad);
  and and_6 (and_6_out, decoder_1_out5, RegLoad);
  and and_7 (and_7_out, decoder_1_out6, RegLoad);
  and and_8 (and_8_out, decoder_1_out7, RegLoad);
  REGISTER_32_Bit Register_0 (.LOAD(and_1_out), .Input(Data_In), .Output(DOUT1));
  REGISTER_32_Bit Register_1 (.LOAD(and_2_out), .Input(Data_In), .Output(DOUT2));
  REGISTER_32_Bit Register_2 (.LOAD(and_3_out), .Input(Data_In), .Output(DOUT3));
  REGISTER_32_Bit Register_3 (.LOAD(and_4_out), .Input(Data_In), .Output(DOUT4));
  REGISTER_32_Bit Register_4 (.LOAD(and_5_out), .Input(Data_In), .Output(DOUT5));
  REGISTER_32_Bit Register_5 (.LOAD(and_6_out), .Input(Data_In), .Output(DOUT6));
  REGISTER_32_Bit Register_6 (.LOAD(and_7_out), .Input(Data_In), .Output(DOUT7));
  INC_DEC_REG_32_Bit REGISTER_7 (
    .REG_LOAD(and_8_out), .REG_INPUT(Data_In), .SPpp(SPpp), .SPnn(SPnn), .REG_OUTPUT(DOUT8));
endmodule

module REGISTER_32_Bit (
  input  [31:0] Input,
  input  LOAD,
  output [31:0] Output
);

  wire and_1_out, and_2_out, and_3_out, and_4_out, and_5_out, and_6_out, and_7_out, and_8_out, and_9_out,
       and_10_out, and_11_out, and_12_out, and_13_out, and_14_out, and_15_out, and_16_out, and_17_out,
       and_18_out, and_19_out, and_20_out, and_21_out, and_22_out, and_23_out, and_24_out, and_25_out,
       and_26_out, and_27_out, and_28_out, and_29_out, and_30_out, and_31_out, and_32_out, and_33_out,
       and_34_out, and_35_out, and_36_out, and_37_out, and_38_out, and_39_out, and_40_out, and_41_out,
       and_42_out, and_43_out, and_44_out, and_45_out, and_46_out, and_47_out, and_48_out, and_49_out,
       and_50_out, and_51_out, and_52_out, and_53_out, and_54_out, and_55_out, and_56_out, and_57_out,
       and_58_out, and_59_out, and_60_out, and_61_out, and_62_out, and_63_out, and_64_out, CLK_out, undriven,
       undriven_2, undriven_3, undriven_4, undriven_5, undriven_6, undriven_7, undriven_8, undriven_9,
       undriven_10, undriven_11, undriven_12;

  and and_1 (and_1_out, Input[0], LOAD);
  and and_2 (and_2_out, ~Input[0], LOAD);  // AND_Gate
  and and_3 (and_3_out, Input[1], LOAD);
  and and_4 (and_4_out, ~Input[1], LOAD);  // AND_Gate
  and and_5 (and_5_out, Input[2], LOAD);
  and and_6 (and_6_out, ~Input[2], LOAD);  // AND_Gate
  and and_7 (and_7_out, Input[3], LOAD);
  and and_8 (and_8_out, ~Input[3], LOAD);  // AND_Gate
  and and_9 (and_9_out, Input[4], LOAD);
  and and_10 (and_10_out, ~Input[4], LOAD);  // AND_Gate
  and and_11 (and_11_out, Input[5], LOAD);
  and and_12 (and_12_out, ~Input[5], LOAD);  // AND_Gate
  and and_13 (and_13_out, Input[6], LOAD);
  and and_14 (and_14_out, ~Input[6], LOAD);  // AND_Gate
  and and_15 (and_15_out, Input[7], LOAD);
  and and_16 (and_16_out, ~Input[7], LOAD);  // AND_Gate
  and and_17 (and_17_out, Input[8], LOAD);
  and and_18 (and_18_out, ~Input[8], LOAD);  // AND_Gate
  and and_19 (and_19_out, Input[9], LOAD);
  and and_20 (and_20_out, ~Input[9], LOAD);  // AND_Gate
  and and_21 (and_21_out, Input[10], LOAD);
  and and_22 (and_22_out, ~Input[10], LOAD);  // AND_Gate
  and and_23 (and_23_out, Input[11], LOAD);
  and and_24 (and_24_out, ~Input[11], LOAD);  // AND_Gate
  and and_25 (and_25_out, Input[12], LOAD);
  and and_26 (and_26_out, ~Input[12], LOAD);  // AND_Gate
  and and_27 (and_27_out, Input[13], LOAD);
  and and_28 (and_28_out, ~Input[13], LOAD);  // AND_Gate
  and and_29 (and_29_out, Input[14], LOAD);
  and and_30 (and_30_out, ~Input[14], LOAD);  // AND_Gate
  and and_31 (and_31_out, Input[15], LOAD);
  and and_32 (and_32_out, ~Input[15], LOAD);  // AND_Gate
  and and_33 (and_33_out, Input[16], LOAD);
  and and_34 (and_34_out, ~Input[16], LOAD);  // AND_Gate
  and and_35 (and_35_out, Input[17], LOAD);
  and and_36 (and_36_out, ~Input[17], LOAD);  // AND_Gate
  and and_37 (and_37_out, Input[18], LOAD);
  and and_38 (and_38_out, ~Input[18], LOAD);  // AND_Gate
  and and_39 (and_39_out, Input[19], LOAD);
  and and_40 (and_40_out, ~Input[19], LOAD);  // AND_Gate
  and and_41 (and_41_out, Input[20], LOAD);
  and and_42 (and_42_out, ~Input[20], LOAD);  // AND_Gate
  and and_43 (and_43_out, Input[21], LOAD);
  and and_44 (and_44_out, ~Input[21], LOAD);  // AND_Gate
  and and_45 (and_45_out, Input[22], LOAD);
  and and_46 (and_46_out, ~Input[22], LOAD);  // AND_Gate
  and and_47 (and_47_out, Input[23], LOAD);
  and and_48 (and_48_out, ~Input[23], LOAD);  // AND_Gate
  and and_49 (and_49_out, Input[24], LOAD);
  and and_50 (and_50_out, ~Input[24], LOAD);  // AND_Gate
  and and_51 (and_51_out, Input[25], LOAD);
  and and_52 (and_52_out, ~Input[25], LOAD);  // AND_Gate
  and and_53 (and_53_out, Input[26], LOAD);
  and and_54 (and_54_out, ~Input[26], LOAD);  // AND_Gate
  and and_55 (and_55_out, Input[27], LOAD);
  and and_56 (and_56_out, ~Input[27], LOAD);  // AND_Gate
  and and_57 (and_57_out, Input[28], LOAD);
  and and_58 (and_58_out, ~Input[28], LOAD);  // AND_Gate
  and and_59 (and_59_out, Input[29], LOAD);
  and and_60 (and_60_out, ~Input[29], LOAD);  // AND_Gate
  and and_61 (and_61_out, Input[30], LOAD);
  and and_62 (and_62_out, ~Input[30], LOAD);  // AND_Gate
  and and_63 (and_63_out, Input[31], LOAD);
  and and_64 (and_64_out, ~Input[31], LOAD);  // AND_Gate
  S_R_Flip_Flop s_r_ff_1 (.S(and_1_out), .R(and_2_out), .clk(CLK_out), .Q(Output[0]));  // open: reset, Qn, preset
  S_R_Flip_Flop s_r_ff_2 (.S(and_3_out), .R(and_4_out), .clk(CLK_out), .Q(Output[1]));  // open: reset, Qn, preset
  S_R_Flip_Flop s_r_ff_3 (.S(and_5_out), .R(and_6_out), .clk(CLK_out), .Q(Output[2]));  // open: reset, Qn, preset
  S_R_Flip_Flop s_r_ff_4 (.S(and_7_out), .R(and_8_out), .clk(CLK_out), .Q(Output[3]));  // open: reset, Qn, preset
  S_R_Flip_Flop s_r_ff_5 (.S(and_9_out), .R(and_10_out), .clk(CLK_out), .Q(Output[4]));  // open: reset, Qn, preset
  S_R_Flip_Flop s_r_ff_6 (.S(and_11_out), .R(and_12_out), .clk(CLK_out), .Q(Output[5]));  // open: reset, Qn, preset
  S_R_Flip_Flop s_r_ff_7 (.S(and_13_out), .R(and_14_out), .clk(CLK_out), .Q(Output[6]));  // open: reset, Qn, preset
  S_R_Flip_Flop s_r_ff_8 (.S(and_15_out), .R(and_16_out), .clk(CLK_out), .Q(Output[7]));  // open: reset, Qn, preset
  S_R_Flip_Flop s_r_ff_9 (.S(and_17_out), .R(and_18_out), .clk(CLK_out), .Q(Output[8]));  // open: reset, Qn, preset
  S_R_Flip_Flop s_r_ff_10 (.S(and_19_out), .R(and_20_out), .clk(CLK_out), .Q(Output[9]));  // open: reset, Qn, preset
  S_R_Flip_Flop s_r_ff_11 (.S(and_21_out), .R(and_22_out), .clk(CLK_out), .Q(Output[10]));  // open: reset, Qn, preset
  S_R_Flip_Flop s_r_ff_12 (.S(and_23_out), .R(and_24_out), .clk(CLK_out), .Q(Output[11]));  // open: reset, Qn, preset
  S_R_Flip_Flop s_r_ff_13 (.S(and_25_out), .R(and_26_out), .clk(CLK_out), .Q(Output[12]));  // open: reset, Qn, preset
  S_R_Flip_Flop s_r_ff_14 (.S(and_27_out), .R(and_28_out), .clk(CLK_out), .Q(Output[13]));  // open: reset, Qn, preset
  S_R_Flip_Flop s_r_ff_15 (.S(and_29_out), .R(and_30_out), .clk(CLK_out), .Q(Output[14]));  // open: reset, Qn, preset
  S_R_Flip_Flop s_r_ff_16 (.S(and_31_out), .R(and_32_out), .clk(CLK_out), .Q(Output[15]));  // open: reset, Qn, preset
  S_R_Flip_Flop s_r_ff_17 (.S(and_33_out), .R(and_34_out), .clk(CLK_out), .Q(Output[16]));  // open: reset, Qn, preset
  S_R_Flip_Flop s_r_ff_18 (.S(and_35_out), .R(and_36_out), .clk(CLK_out), .Q(Output[17]));  // open: reset, Qn, preset
  S_R_Flip_Flop s_r_ff_19 (.S(and_37_out), .R(and_38_out), .clk(CLK_out), .Q(Output[18]));  // open: reset, Qn, preset
  S_R_Flip_Flop s_r_ff_20 (.S(and_39_out), .R(and_40_out), .clk(CLK_out), .Q(Output[19]));  // open: reset, Qn, preset
  S_R_Flip_Flop s_r_ff_21 (
    .S(and_41_out), .R(and_42_out), .clk(CLK_out), .Q(Output[20]), .preset(undriven));  // open: reset, Qn
  S_R_Flip_Flop s_r_ff_22 (
    .S(and_43_out), .R(and_44_out), .clk(CLK_out), .Q(Output[21]), .preset(undriven_2));  // open: reset, Qn
  S_R_Flip_Flop s_r_ff_23 (
    .S(and_45_out), .R(and_46_out), .clk(CLK_out), .Q(Output[22]), .preset(undriven_3));  // open: reset, Qn
  S_R_Flip_Flop s_r_ff_24 (
    .S(and_47_out), .R(and_48_out), .clk(CLK_out), .Q(Output[23]), .preset(undriven_4));  // open: reset, Qn
  S_R_Flip_Flop s_r_ff_25 (
    .S(and_49_out), .R(and_50_out), .clk(CLK_out), .Q(Output[24]), .preset(undriven_5));  // open: reset, Qn
  S_R_Flip_Flop s_r_ff_26 (
    .S(and_51_out), .R(and_52_out), .clk(CLK_out), .Q(Output[25]), .preset(undriven_6));  // open: reset, Qn
  S_R_Flip_Flop s_r_ff_27 (
    .S(and_53_out), .R(and_54_out), .clk(CLK_out), .Q(Output[26]), .preset(undriven_7));  // open: reset, Qn
  S_R_Flip_Flop s_r_ff_28 (
    .S(and_55_out), .R(and_56_out), .clk(CLK_out), .Q(Output[27]), .preset(undriven_8));  // open: reset, Qn
  S_R_Flip_Flop s_r_ff_29 (
    .S(and_57_out), .R(and_58_out), .clk(CLK_out), .Q(Output[28]), .preset(undriven_9));  // open: reset, Qn
  S_R_Flip_Flop s_r_ff_30 (
    .S(and_59_out), .R(and_60_out), .clk(CLK_out), .Q(Output[29]), .preset(undriven_10));  // open: reset, Qn
  S_R_Flip_Flop s_r_ff_31 (
    .S(and_61_out), .R(and_62_out), .clk(CLK_out), .Q(Output[30]), .preset(undriven_11));  // open: reset, Qn
  S_R_Flip_Flop s_r_ff_32 (
    .S(and_63_out), .R(and_64_out), .clk(CLK_out), .Q(Output[31]), .preset(undriven_12));  // open: reset, Qn
  Clock CLK (.out(CLK_out));
endmodule

module ALU_32_Bit (
  input  [31:0] Input_1,
  input  [31:0] Input_2,
  input  [4:0] ALUCODE,
  output OVERFLOW,
  output [31:0] OUTPUT,
  output LESS_THAN,
  output GREATER_THAN,
  output EQUAL,
  output NOT_EQUAL,
  output GREATER_OR_EQUAL,
  output LESS_OR_EQUAL
);

  wire adder_1_cout, adder_2_cout, not_1_out;
  wire [31:0] adder_1_out, adder_2_out, and_1_out, not_2_out, or_2_out, subtractor_1_out, subtractor_2_out,
       xor_1_out;

  not not_1 (not_1_out, LESS_THAN);
  or or_1 (LESS_OR_EQUAL, LESS_THAN, EQUAL);
  Adder #(.width(32)) adder_1 (.a(Input_1), .b(Input_2), .out(adder_1_out), .cout(adder_1_cout));  // open: cin
  Subtractor #(.width(32)) subtractor_1 (
    .a(Input_1), .b(Input_2), .out(subtractor_1_out), .bout(LESS_THAN));  // open: bin
  assign and_1_out = Input_1 & Input_2;  // AND_Gate and_1, 32 bits wide
  assign or_2_out = Input_1 | Input_2;  // OR_Gate or_2, 32 bits wide
  assign xor_1_out = Input_1 ^ Input_2;  // XOR_Gate xor_1, 32 bits wide
  assign not_2_out = ~Input_1;  // NOT_Gate not_2, 32 bits wide
  Adder #(.width(32)) adder_2 (.a(Input_1), .b(32'h1), .out(adder_2_out), .cout(adder_2_cout));  // open: cin
  Subtractor #(.width(32)) subtractor_2 (.a(Input_1), .b(32'h1), .out(subtractor_2_out));  // open: bin, bout
  or or_3 (OVERFLOW, adder_1_cout, adder_2_cout);
  and and_2 (GREATER_THAN, not_1_out, NOT_EQUAL);
  or or_4 (GREATER_OR_EQUAL, GREATER_THAN, EQUAL);
  or or_5 (NOT_EQUAL, subtractor_1_out[31], subtractor_1_out[30], subtractor_1_out[29], subtractor_1_out[28], subtractor_1_out[27], subtractor_1_out[26], subtractor_1_out[25], subtractor_1_out[24], subtractor_1_out[23], subtractor_1_out[22], subtractor_1_out[21], subtractor_1_out[20], subtractor_1_out[19], subtractor_1_out[18], subtractor_1_out[17], subtractor_1_out[16], subtractor_1_out[15], subtractor_1_out[14], subtractor_1_out[13], subtractor_1_out[12], subtractor_1_out[11], subtractor_1_out[10], subtractor_1_out[9], subtractor_1_out[8], subtractor_1_out[7], subtractor_1_out[6], subtractor_1_out[5], subtractor_1_out[4], subtractor_1_out[3], subtractor_1_out[2], subtractor_1_out[1], subtractor_1_out[0]);
  not not_3 (EQUAL, NOT_EQUAL);
  Multiplexer #(.select(5), .width(32)) multiplexer_1 (
    .in0(adder_1_out), .in1(subtractor_1_out), .in2(and_1_out), .in3(or_2_out), .in4(xor_1_out),
    .in5(not_2_out), .in6(Input_1), .in7(adder_2_out), .in8(subtractor_2_out), .out(OUTPUT), .sel(ALUCODE));  // open: in9, in10, in11, in12, in13, in14, in15, in16, in17, in18, in19, in20, in21, in22, in23, in24, in25, in26, in27, in28, in29, in30, in31
endmodule

module INC_DEC_REG_32_Bit (
  input  SPpp,
  input  SPnn,
  input  [31:0] REG_INPUT,
  input  REG_LOAD,
  output [31:0] REG_OUTPUT
);

  wire [31:0] adder_1_out, multiplexer_1_out, multiplexer_2_out, subtractor_1_out;

  Multiplexer #(.width(32)) multiplexer_1 (.in0(REG_INPUT), .in1(adder_1_out), .out(multiplexer_1_out), .sel(SPpp));
  Adder #(.width(32)) adder_1 (.a(32'h1), .b(REG_OUTPUT), .out(adder_1_out));  // open: cin, cout
  Multiplexer #(.width(32)) multiplexer_2 (
    .in0(multiplexer_1_out), .in1(subtractor_1_out), .out(multiplexer_2_out), .sel(SPnn));
  Subtractor #(.width(32)) subtractor_1 (.a(REG_OUTPUT), .b(32'h1), .out(subtractor_1_out));  // open: bin, bout
  REGISTER_32_Bit register_32_bit_1 (.LOAD(REG_LOAD), .Input(multiplexer_2_out), .Output(REG_OUTPUT));
endmodule

module INSTRUCTION_REGISTER (
  input  [27:0] IR_INPUT,
  input  IR_LD,
  output [27:0] IR_OUT
);

  wire and_1_out, and_2_out, and_3_out, and_4_out, and_5_out, and_6_out, and_7_out, and_8_out, and_9_out,
       and_10_out, and_11_out, and_12_out, and_13_out, and_14_out, and_15_out, and_16_out, and_17_out,
       and_18_out, and_19_out, and_20_out, and_21_out, and_22_out, and_23_out, and_24_out, and_25_out,
       and_26_out, and_27_out, and_28_out, and_29_out, and_30_out, and_31_out, and_32_out, and_33_out,
       and_34_out, and_35_out, and_36_out, and_37_out, and_38_out, and_39_out, and_40_out, and_41_out,
       and_42_out, and_43_out, and_44_out, and_45_out, and_46_out, and_47_out, and_48_out, and_49_out,
       and_50_out, and_51_out, and_52_out, and_53_out, and_54_out, and_55_out, and_56_out, clock_1_out,
       undriven, undriven_2, undriven_3, undriven_4, undriven_5, undriven_6, undriven_7, undriven_8;

  and and_1 (and_1_out, IR_INPUT[0], IR_LD);
  and and_2 (and_2_out, ~IR_INPUT[0], IR_LD);  // AND_Gate
  and and_3 (and_3_out, IR_INPUT[1], IR_LD);
  and and_4 (and_4_out, ~IR_INPUT[1], IR_LD);  // AND_Gate
  and and_5 (and_5_out, IR_INPUT[2], IR_LD);
  and and_6 (and_6_out, ~IR_INPUT[2], IR_LD);  // AND_Gate
  and and_7 (and_7_out, IR_INPUT[3], IR_LD);
  and and_8 (and_8_out, ~IR_INPUT[3], IR_LD);  // AND_Gate
  and and_9 (and_9_out, IR_INPUT[4], IR_LD);
  and and_10 (and_10_out, ~IR_INPUT[4], IR_LD);  // AND_Gate
  and and_11 (and_11_out, IR_INPUT[5], IR_LD);
  and and_12 (and_12_out, ~IR_INPUT[5], IR_LD);  // AND_Gate
  and and_13 (and_13_out, IR_INPUT[6], IR_LD);
  and and_14 (and_14_out, ~IR_INPUT[6], IR_LD);  // AND_Gate
  and and_15 (and_15_out, IR_INPUT[7], IR_LD);
  and and_16 (and_16_out, ~IR_INPUT[7], IR_LD);  // AND_Gate
  and and_17 (and_17_out, IR_INPUT[8], IR_LD);
  and and_18 (and_18_out, ~IR_INPUT[8], IR_LD);  // AND_Gate
  and and_19 (and_19_out, IR_INPUT[9], IR_LD);
  and and_20 (and_20_out, ~IR_INPUT[9], IR_LD);  // AND_Gate
  and and_21 (and_21_out, IR_INPUT[10], IR_LD);
  and and_22 (and_22_out, ~IR_INPUT[10], IR_LD);  // AND_Gate
  and and_23 (and_23_out, IR_INPUT[11], IR_LD);
  and and_24 (and_24_out, ~IR_INPUT[11], IR_LD);  // AND_Gate
  and and_25 (and_25_out, IR_INPUT[12], IR_LD);
  and and_26 (and_26_out, ~IR_INPUT[12], IR_LD);  // AND_Gate
  and and_27 (and_27_out, IR_INPUT[13], IR_LD);
  and and_28 (and_28_out, ~IR_INPUT[13], IR_LD);  // AND_Gate
  and and_29 (and_29_out, IR_INPUT[14], IR_LD);
  and and_30 (and_30_out, ~IR_INPUT[14], IR_LD);  // AND_Gate
  and and_31 (and_31_out, IR_INPUT[15], IR_LD);
  and and_32 (and_32_out, ~IR_INPUT[15], IR_LD);  // AND_Gate
  and and_33 (and_33_out, IR_INPUT[16], IR_LD);
  and and_34 (and_34_out, ~IR_INPUT[16], IR_LD);  // AND_Gate
  and and_35 (and_35_out, IR_INPUT[17], IR_LD);
  and and_36 (and_36_out, ~IR_INPUT[17], IR_LD);  // AND_Gate
  and and_37 (and_37_out, IR_INPUT[18], IR_LD);
  and and_38 (and_38_out, ~IR_INPUT[18], IR_LD);  // AND_Gate
  and and_39 (and_39_out, IR_INPUT[19], IR_LD);
  and and_40 (and_40_out, ~IR_INPUT[19], IR_LD);  // AND_Gate
  and and_41 (and_41_out, IR_INPUT[20], IR_LD);
  and and_42 (and_42_out, ~IR_INPUT[20], IR_LD);  // AND_Gate
  and and_43 (and_43_out, IR_INPUT[21], IR_LD);
  and and_44 (and_44_out, ~IR_INPUT[21], IR_LD);  // AND_Gate
  and and_45 (and_45_out, IR_INPUT[22], IR_LD);
  and and_46 (and_46_out, ~IR_INPUT[22], IR_LD);  // AND_Gate
  and and_47 (and_47_out, IR_INPUT[23], IR_LD);
  and and_48 (and_48_out, ~IR_INPUT[23], IR_LD);  // AND_Gate
  and and_49 (and_49_out, IR_INPUT[24], IR_LD);
  and and_50 (and_50_out, ~IR_INPUT[24], IR_LD);  // AND_Gate
  and and_51 (and_51_out, IR_INPUT[25], IR_LD);
  and and_52 (and_52_out, ~IR_INPUT[25], IR_LD);  // AND_Gate
  and and_53 (and_53_out, IR_INPUT[26], IR_LD);
  and and_54 (and_54_out, ~IR_INPUT[26], IR_LD);  // AND_Gate
  and and_55 (and_55_out, IR_INPUT[27], IR_LD);
  and and_56 (and_56_out, ~IR_INPUT[27], IR_LD);  // AND_Gate
  S_R_Flip_Flop s_r_ff_1 (.S(and_1_out), .R(and_2_out), .clk(clock_1_out), .Q(IR_OUT[0]));  // open: reset, Qn, preset
  S_R_Flip_Flop s_r_ff_2 (.S(and_3_out), .R(and_4_out), .clk(clock_1_out), .Q(IR_OUT[1]));  // open: reset, Qn, preset
  S_R_Flip_Flop s_r_ff_3 (.S(and_5_out), .R(and_6_out), .clk(clock_1_out), .Q(IR_OUT[2]));  // open: reset, Qn, preset
  S_R_Flip_Flop s_r_ff_4 (.S(and_7_out), .R(and_8_out), .clk(clock_1_out), .Q(IR_OUT[3]));  // open: reset, Qn, preset
  S_R_Flip_Flop s_r_ff_5 (.S(and_9_out), .R(and_10_out), .clk(clock_1_out), .Q(IR_OUT[4]));  // open: reset, Qn, preset
  S_R_Flip_Flop s_r_ff_6 (.S(and_11_out), .R(and_12_out), .clk(clock_1_out), .Q(IR_OUT[5]));  // open: reset, Qn, preset
  S_R_Flip_Flop s_r_ff_7 (.S(and_13_out), .R(and_14_out), .clk(clock_1_out), .Q(IR_OUT[6]));  // open: reset, Qn, preset
  S_R_Flip_Flop s_r_ff_8 (.S(and_15_out), .R(and_16_out), .clk(clock_1_out), .Q(IR_OUT[7]));  // open: reset, Qn, preset
  S_R_Flip_Flop s_r_ff_9 (.S(and_17_out), .R(and_18_out), .clk(clock_1_out), .Q(IR_OUT[8]));  // open: reset, Qn, preset
  S_R_Flip_Flop s_r_ff_10 (
    .S(and_19_out), .R(and_20_out), .clk(clock_1_out), .Q(IR_OUT[9]));  // open: reset, Qn, preset
  S_R_Flip_Flop s_r_ff_11 (
    .S(and_21_out), .R(and_22_out), .clk(clock_1_out), .Q(IR_OUT[10]));  // open: reset, Qn, preset
  S_R_Flip_Flop s_r_ff_12 (
    .S(and_23_out), .R(and_24_out), .clk(clock_1_out), .Q(IR_OUT[11]));  // open: reset, Qn, preset
  S_R_Flip_Flop s_r_ff_13 (
    .S(and_25_out), .R(and_26_out), .clk(clock_1_out), .Q(IR_OUT[12]));  // open: reset, Qn, preset
  S_R_Flip_Flop s_r_ff_14 (
    .S(and_27_out), .R(and_28_out), .clk(clock_1_out), .Q(IR_OUT[13]));  // open: reset, Qn, preset
  S_R_Flip_Flop s_r_ff_15 (
    .S(and_29_out), .R(and_30_out), .clk(clock_1_out), .Q(IR_OUT[14]));  // open: reset, Qn, preset
  S_R_Flip_Flop s_r_ff_16 (
    .S(and_31_out), .R(and_32_out), .clk(clock_1_out), .Q(IR_OUT[15]));  // open: reset, Qn, preset
  S_R_Flip_Flop s_r_ff_17 (
    .S(and_33_out), .R(and_34_out), .clk(clock_1_out), .Q(IR_OUT[16]));  // open: reset, Qn, preset
  S_R_Flip_Flop s_r_ff_18 (
    .S(and_35_out), .R(and_36_out), .clk(clock_1_out), .Q(IR_OUT[17]));  // open: reset, Qn, preset
  S_R_Flip_Flop s_r_ff_19 (
    .S(and_37_out), .R(and_38_out), .clk(clock_1_out), .Q(IR_OUT[18]));  // open: reset, Qn, preset
  S_R_Flip_Flop s_r_ff_20 (
    .S(and_39_out), .R(and_40_out), .clk(clock_1_out), .Q(IR_OUT[19]));  // open: reset, Qn, preset
  S_R_Flip_Flop s_r_ff_21 (
    .S(and_41_out), .R(and_42_out), .clk(clock_1_out), .Q(IR_OUT[20]), .preset(undriven));  // open: reset, Qn
  S_R_Flip_Flop s_r_ff_22 (
    .S(and_43_out), .R(and_44_out), .clk(clock_1_out), .Q(IR_OUT[21]), .preset(undriven_2));  // open: reset, Qn
  S_R_Flip_Flop s_r_ff_23 (
    .S(and_45_out), .R(and_46_out), .clk(clock_1_out), .Q(IR_OUT[22]), .preset(undriven_3));  // open: reset, Qn
  S_R_Flip_Flop s_r_ff_24 (
    .S(and_47_out), .R(and_48_out), .clk(clock_1_out), .Q(IR_OUT[23]), .preset(undriven_4));  // open: reset, Qn
  S_R_Flip_Flop s_r_ff_25 (
    .S(and_49_out), .R(and_50_out), .clk(clock_1_out), .Q(IR_OUT[24]), .preset(undriven_5));  // open: reset, Qn
  S_R_Flip_Flop s_r_ff_26 (
    .S(and_51_out), .R(and_52_out), .clk(clock_1_out), .Q(IR_OUT[25]), .preset(undriven_6));  // open: reset, Qn
  S_R_Flip_Flop s_r_ff_27 (
    .S(and_53_out), .R(and_54_out), .clk(clock_1_out), .Q(IR_OUT[26]), .preset(undriven_7));  // open: reset, Qn
  S_R_Flip_Flop s_r_ff_28 (
    .S(and_55_out), .R(and_56_out), .clk(clock_1_out), .Q(IR_OUT[27]), .preset(undriven_8));  // open: reset, Qn
  Clock clock_1 (.out(clock_1_out));
endmodule

module ProgramCounter (
  input  [27:0] IR_INPUT,
  input  PC_INC,
  input  PC_LD,
  output [27:0] IR_OUT
);

  wire and_1_out, and_2_out, and_3_out, and_4_out, and_5_out, and_6_out, and_7_out, and_8_out, and_9_out,
       and_10_out, and_11_out, and_12_out, and_13_out, and_14_out, and_15_out, and_16_out, and_17_out,
       and_18_out, and_19_out, and_20_out, and_21_out, and_22_out, and_23_out, and_24_out, and_25_out,
       and_26_out, and_27_out, and_28_out, and_29_out, and_30_out, and_31_out, and_32_out, and_33_out,
       and_34_out, and_35_out, and_36_out, and_37_out, and_38_out, and_39_out, and_40_out, and_41_out,
       and_42_out, and_43_out, and_44_out, and_45_out, and_46_out, and_47_out, and_48_out, and_49_out,
       and_50_out, and_51_out, and_52_out, and_53_out, and_54_out, and_55_out, and_56_out, clock_1_out,
       undriven, undriven_2, undriven_3, undriven_4, undriven_5, undriven_6, undriven_7, undriven_8;
  wire [27:0] adder_1_out, multiplexer_1_out;

  Multiplexer #(.width(28)) multiplexer_1 (.in0(IR_INPUT), .in1(adder_1_out), .out(multiplexer_1_out), .sel(PC_INC));
  Adder #(.width(28)) adder_1 (.a(28'h1), .b(IR_OUT), .out(adder_1_out));  // open: cin, cout
  and and_1 (and_1_out, multiplexer_1_out[0], PC_LD);
  and and_2 (and_2_out, ~multiplexer_1_out[0], PC_LD);  // AND_Gate
  and and_3 (and_3_out, multiplexer_1_out[1], PC_LD);
  and and_4 (and_4_out, ~multiplexer_1_out[1], PC_LD);  // AND_Gate
  and and_5 (and_5_out, multiplexer_1_out[2], PC_LD);
  and and_6 (and_6_out, ~multiplexer_1_out[2], PC_LD);  // AND_Gate
  and and_7 (and_7_out, multiplexer_1_out[3], PC_LD);
  and and_8 (and_8_out, ~multiplexer_1_out[3], PC_LD);  // AND_Gate
  and and_9 (and_9_out, multiplexer_1_out[4], PC_LD);
  and and_10 (and_10_out, ~multiplexer_1_out[4], PC_LD);  // AND_Gate
  and and_11 (and_11_out, multiplexer_1_out[5], PC_LD);
  and and_12 (and_12_out, ~multiplexer_1_out[5], PC_LD);  // AND_Gate
  and and_13 (and_13_out, multiplexer_1_out[6], PC_LD);
  and and_14 (and_14_out, ~multiplexer_1_out[6], PC_LD);  // AND_Gate
  and and_15 (and_15_out, multiplexer_1_out[7], PC_LD);
  and and_16 (and_16_out, ~multiplexer_1_out[7], PC_LD);  // AND_Gate
  and and_17 (and_17_out, multiplexer_1_out[8], PC_LD);
  and and_18 (and_18_out, ~multiplexer_1_out[8], PC_LD);  // AND_Gate
  and and_19 (and_19_out, multiplexer_1_out[9], PC_LD);
  and and_20 (and_20_out, ~multiplexer_1_out[9], PC_LD);  // AND_Gate
  and and_21 (and_21_out, multiplexer_1_out[10], PC_LD);
  and and_22 (and_22_out, ~multiplexer_1_out[10], PC_LD);  // AND_Gate
  and and_23 (and_23_out, multiplexer_1_out[11], PC_LD);
  and and_24 (and_24_out, ~multiplexer_1_out[11], PC_LD);  // AND_Gate
  and and_25 (and_25_out, multiplexer_1_out[12], PC_LD);
  and and_26 (and_26_out, ~multiplexer_1_out[12], PC_LD);  // AND_Gate
  and and_27 (and_27_out, multiplexer_1_out[13], PC_LD);
  and and_28 (and_28_out, ~multiplexer_1_out[13], PC_LD);  // AND_Gate
  and and_29 (and_29_out, multiplexer_1_out[14], PC_LD);
  and and_30 (and_30_out, ~multiplexer_1_out[14], PC_LD);  // AND_Gate
  and and_31 (and_31_out, multiplexer_1_out[15], PC_LD);
  and and_32 (and_32_out, ~multiplexer_1_out[15], PC_LD);  // AND_Gate
  and and_33 (and_33_out, multiplexer_1_out[16], PC_LD);
  and and_34 (and_34_out, ~multiplexer_1_out[16], PC_LD);  // AND_Gate
  and and_35 (and_35_out, multiplexer_1_out[17], PC_LD);
  and and_36 (and_36_out, ~multiplexer_1_out[17], PC_LD);  // AND_Gate
  and and_37 (and_37_out, multiplexer_1_out[18], PC_LD);
  and and_38 (and_38_out, ~multiplexer_1_out[18], PC_LD);  // AND_Gate
  and and_39 (and_39_out, multiplexer_1_out[19], PC_LD);
  and and_40 (and_40_out, ~multiplexer_1_out[19], PC_LD);  // AND_Gate
  and and_41 (and_41_out, multiplexer_1_out[20], PC_LD);
  and and_42 (and_42_out, ~multiplexer_1_out[20], PC_LD);  // AND_Gate
  and and_43 (and_43_out, multiplexer_1_out[21], PC_LD);
  and and_44 (and_44_out, ~multiplexer_1_out[21], PC_LD);  // AND_Gate
  and and_45 (and_45_out, multiplexer_1_out[22], PC_LD);
  and and_46 (and_46_out, ~multiplexer_1_out[22], PC_LD);  // AND_Gate
  and and_47 (and_47_out, multiplexer_1_out[23], PC_LD);
  and and_48 (and_48_out, ~multiplexer_1_out[23], PC_LD);  // AND_Gate
  and and_49 (and_49_out, multiplexer_1_out[24], PC_LD);
  and and_50 (and_50_out, ~multiplexer_1_out[24], PC_LD);  // AND_Gate
  and and_51 (and_51_out, multiplexer_1_out[25], PC_LD);
  and and_52 (and_52_out, ~multiplexer_1_out[25], PC_LD);  // AND_Gate
  and and_53 (and_53_out, multiplexer_1_out[26], PC_LD);
  and and_54 (and_54_out, ~multiplexer_1_out[26], PC_LD);  // AND_Gate
  and and_55 (and_55_out, multiplexer_1_out[27], PC_LD);
  and and_56 (and_56_out, ~multiplexer_1_out[27], PC_LD);  // AND_Gate
  S_R_Flip_Flop s_r_ff_1 (.S(and_1_out), .R(and_2_out), .clk(clock_1_out), .Q(IR_OUT[0]));  // open: reset, Qn, preset
  S_R_Flip_Flop s_r_ff_2 (.S(and_3_out), .R(and_4_out), .clk(clock_1_out), .Q(IR_OUT[1]));  // open: reset, Qn, preset
  S_R_Flip_Flop s_r_ff_3 (.S(and_5_out), .R(and_6_out), .clk(clock_1_out), .Q(IR_OUT[2]));  // open: reset, Qn, preset
  S_R_Flip_Flop s_r_ff_4 (.S(and_7_out), .R(and_8_out), .clk(clock_1_out), .Q(IR_OUT[3]));  // open: reset, Qn, preset
  S_R_Flip_Flop s_r_ff_5 (.S(and_9_out), .R(and_10_out), .clk(clock_1_out), .Q(IR_OUT[4]));  // open: reset, Qn, preset
  S_R_Flip_Flop s_r_ff_6 (.S(and_11_out), .R(and_12_out), .clk(clock_1_out), .Q(IR_OUT[5]));  // open: reset, Qn, preset
  S_R_Flip_Flop s_r_ff_7 (.S(and_13_out), .R(and_14_out), .clk(clock_1_out), .Q(IR_OUT[6]));  // open: reset, Qn, preset
  S_R_Flip_Flop s_r_ff_8 (.S(and_15_out), .R(and_16_out), .clk(clock_1_out), .Q(IR_OUT[7]));  // open: reset, Qn, preset
  S_R_Flip_Flop s_r_ff_9 (.S(and_17_out), .R(and_18_out), .clk(clock_1_out), .Q(IR_OUT[8]));  // open: reset, Qn, preset
  S_R_Flip_Flop s_r_ff_10 (
    .S(and_19_out), .R(and_20_out), .clk(clock_1_out), .Q(IR_OUT[9]));  // open: reset, Qn, preset
  S_R_Flip_Flop s_r_ff_11 (
    .S(and_21_out), .R(and_22_out), .clk(clock_1_out), .Q(IR_OUT[10]));  // open: reset, Qn, preset
  S_R_Flip_Flop s_r_ff_12 (
    .S(and_23_out), .R(and_24_out), .clk(clock_1_out), .Q(IR_OUT[11]));  // open: reset, Qn, preset
  S_R_Flip_Flop s_r_ff_13 (
    .S(and_25_out), .R(and_26_out), .clk(clock_1_out), .Q(IR_OUT[12]));  // open: reset, Qn, preset
  S_R_Flip_Flop s_r_ff_14 (
    .S(and_27_out), .R(and_28_out), .clk(clock_1_out), .Q(IR_OUT[13]));  // open: reset, Qn, preset
  S_R_Flip_Flop s_r_ff_15 (
    .S(and_29_out), .R(and_30_out), .clk(clock_1_out), .Q(IR_OUT[14]));  // open: reset, Qn, preset
  S_R_Flip_Flop s_r_ff_16 (
    .S(and_31_out), .R(and_32_out), .clk(clock_1_out), .Q(IR_OUT[15]));  // open: reset, Qn, preset
  S_R_Flip_Flop s_r_ff_17 (
    .S(and_33_out), .R(and_34_out), .clk(clock_1_out), .Q(IR_OUT[16]));  // open: reset, Qn, preset
  S_R_Flip_Flop s_r_ff_18 (
    .S(and_35_out), .R(and_36_out), .clk(clock_1_out), .Q(IR_OUT[17]));  // open: reset, Qn, preset
  S_R_Flip_Flop s_r_ff_19 (
    .S(and_37_out), .R(and_38_out), .clk(clock_1_out), .Q(IR_OUT[18]));  // open: reset, Qn, preset
  S_R_Flip_Flop s_r_ff_20 (
    .S(and_39_out), .R(and_40_out), .clk(clock_1_out), .Q(IR_OUT[19]));  // open: reset, Qn, preset
  S_R_Flip_Flop s_r_ff_21 (
    .S(and_41_out), .R(and_42_out), .clk(clock_1_out), .Q(IR_OUT[20]), .preset(undriven));  // open: reset, Qn
  S_R_Flip_Flop s_r_ff_22 (
    .S(and_43_out), .R(and_44_out), .clk(clock_1_out), .Q(IR_OUT[21]), .preset(undriven_2));  // open: reset, Qn
  S_R_Flip_Flop s_r_ff_23 (
    .S(and_45_out), .R(and_46_out), .clk(clock_1_out), .Q(IR_OUT[22]), .preset(undriven_3));  // open: reset, Qn
  S_R_Flip_Flop s_r_ff_24 (
    .S(and_47_out), .R(and_48_out), .clk(clock_1_out), .Q(IR_OUT[23]), .preset(undriven_4));  // open: reset, Qn
  S_R_Flip_Flop s_r_ff_25 (
    .S(and_49_out), .R(and_50_out), .clk(clock_1_out), .Q(IR_OUT[24]), .preset(undriven_5));  // open: reset, Qn
  S_R_Flip_Flop s_r_ff_26 (
    .S(and_51_out), .R(and_52_out), .clk(clock_1_out), .Q(IR_OUT[25]), .preset(undriven_6));  // open: reset, Qn
  S_R_Flip_Flop s_r_ff_27 (
    .S(and_53_out), .R(and_54_out), .clk(clock_1_out), .Q(IR_OUT[26]), .preset(undriven_7));  // open: reset, Qn
  S_R_Flip_Flop s_r_ff_28 (
    .S(and_55_out), .R(and_56_out), .clk(clock_1_out), .Q(IR_OUT[27]), .preset(undriven_8));  // open: reset, Qn
  Clock clock_1 (.out(clock_1_out));
endmodule

module FOUR_BIT_EXTENDER (
  input  [27:0] Xtender_input,
  output [31:0] Xtender_output
);


  assign Xtender_output = {4'b0000, Xtender_input};
endmodule

module Thirtyone_BIT_EXTENDER (
  input  Xtender_IN,
  output [31:0] Xtender_out
);


  assign Xtender_out = {{31{1'b0}}, Xtender_IN};
endmodule
