// Logisim project Vertabrate32bit.circ as structural Verilog: 3 circuits, main circuit main
module main (
);

  RegisterBank32 registerbank32_1 ();  // open: RegSelect, RegLoad, Data_In, SP_minus_minus, SP_plus_plus, DOUT1, DOUT2, DOUT3, DOUT4, DOUT5, DOUT6, DOUT7, DOUT8
endmodule

module Vertebrate32 (
);

  main main_1 ();
endmodule

module RegisterBank32 (
  input  [2:0] RegSelect,
  input  RegLoad,
  input  [31:0] Data_In,
  input  SP_plus_plus,
  input  SP_minus_minus,
  output [31:0] DOUT1,
  output [31:0] DOUT2,
  output [31:0] DOUT3,
  output [31:0] DOUT4,
  output [31:0] DOUT5,
  output [31:0] DOUT6,
  output [31:0] DOUT7,
  output [31:0] DOUT8
);

  wire and_1_out, and_2_out, and_3_out, and_4_out, and_5_out, and_6_out, and_7_out, and_8_out, clock_1_out,
       decoder_1_out0, decoder_1_out1, decoder_1_out2, decoder_1_out3, decoder_1_out4, decoder_1_out5,
       decoder_1_out6, decoder_1_out7;
  wire [31:0] adder_1_out, multiplexer_1_out, multiplexer_3_out, subtractor_1_out;

  Clock clock_1 (.out(clock_1_out));
  Decoder #(.select(3)) decoder_1 (
    .out0(decoder_1_out0), .out1(decoder_1_out1), .out2(decoder_1_out2), .out3(decoder_1_out3),
    .out4(decoder_1_out4), .out5(decoder_1_out5), .out6(decoder_1_out6), .out7(decoder_1_out7),
    .sel(RegSelect));  // open: en
  Multiplexer #(.width(32), .enable("false")) multiplexer_1 (
    .in0(Data_In), .in1(subtractor_1_out), .out(multiplexer_1_out), .sel(SP_minus_minus));
  and and_1 (and_1_out, decoder_1_out0, RegLoad);
  and and_2 (and_2_out, decoder_1_out1, RegLoad);
  and and_3 (and_3_out, decoder_1_out2, RegLoad);
  and and_4 (and_4_out, decoder_1_out3, RegLoad);
  and and_5 (and_5_out, decoder_1_out4, RegLoad);
  and and_6 (and_6_out, decoder_1_out5, RegLoad);
  and and_7 (and_7_out, decoder_1_out6, RegLoad);
  and and_8 (and_8_out, decoder_1_out7, RegLoad);
  Subtractor #(.width(32)) subtractor_1 (.a(DOUT8), .b(32'h1), .out(subtractor_1_out));  // open: bin, bout
  Multiplexer #(.width(32), .enable("false")) multiplexer_2 (
    .in0(multiplexer_1_out), .in1(multiplexer_3_out));  // open: out, sel
  Register #(.width(32)) Register_0 (.D(Data_In), .en(and_1_out), .Q(DOUT1), .clk(clock_1_out));  // open: clr
  Register #(.width(32)) Register_1 (.D(Data_In), .en(and_2_out), .Q(DOUT2), .clk(clock_1_out));  // open: clr
  Register #(.width(32)) Register_2 (.D(Data_In), .en(and_3_out), .Q(DOUT3), .clk(clock_1_out));  // open: clr
  Register #(.width(32)) Register_3 (.D(Data_In), .en(and_4_out), .Q(DOUT4), .clk(clock_1_out));  // open: clr
  Register #(.width(32)) Register_4 (.D(Data_In), .en(and_5_out), .Q(DOUT5), .clk(clock_1_out));  // open: clr
  Register #(.width(32)) Register_5 (.D(Data_In), .en(and_6_out), .Q(DOUT6), .clk(clock_1_out));  // open: clr
  Register #(.width(32)) Register_6 (.D(Data_In), .en(and_7_out), .Q(DOUT7), .clk(clock_1_out));  // open: clr
  Register #(.width(32)) Register_7 (.en(and_8_out), .Q(DOUT8), .clk(clock_1_out));  // open: D, clr
  Multiplexer #(.width(32), .enable("false")) multiplexer_3 (
    .in0(Data_In), .in1(adder_1_out), .out(multiplexer_3_out), .sel(SP_plus_plus));
  Adder #(.width(32)) adder_1 (.a(DOUT8), .b(32'h1), .out(adder_1_out));  // open: cin, cout
endmodule
